# Fritzing sketch Car Diagram (saved by Fritzing 0.9.10b)
breadboards: 1

parts:
  Part1 = NRF24L01+ Breakout Board
  Part2 = Arduino Mega ADK (Rev3)
  U1 = L298 [package=multiwatt15]
  M1 = DC Motor [voltage_(max)=6V voltage_(min)=3V]
  M2 = DC Motor [voltage_(max)=6V voltage_(min)=3V]
  M3 = DC Motor [voltage_(max)=6V voltage_(min)=3V]
  M4 = DC Motor [voltage_(max)=6V voltage_(min)=3V]
  IR_Left = Infrared Proximity Sensor [distance_to_obstacle=50%]
  Buzzer_Left = Passive Buzzer
  IR_Right = Infrared Proximity Sensor [distance_to_obstacle=50%]
  Buzzer_Right = Passive Buzzer
  HC-SR04 = HC-SR04 Ultrasonic Distance Sensor
  IR_Front_Left = Infrared Proximity Sensor [distance_to_obstacle=50%]
  IR_Front_Right = Infrared Proximity Sensor [distance_to_obstacle=50%]
  Servomotor = Dagu DGServo 9g (Top view) [part_number=RS001B]
  R1 = PHOTOCELL [package=photocell-kit]
  10_K = Resistor [tolerance=±5% resistance=220 package="0603 [SMD]"]
  U2 = TRANSISTOR_NPN_2 [package=to-92]
  U3 = TRANSISTOR_NPN_2 [package=to-92]
  U4 = TRANSISTOR_NPN_2 [package=to-92]
  U5 = TRANSISTOR_NPN_2 [package=to-92]
  U6 = TRANSISTOR_NPN_2 [package=to-92]
  U7 = TRANSISTOR_NPN_2 [package=to-92]
  U8 = TRANSISTOR_NPN_2 [package=to-92]
  U9 = TRANSISTOR_NPN_2 [package=to-92]
  1_K = Resistor [tolerance=±5% resistance=220 package="0603 [SMD]"]
  1_K_2 = Resistor [tolerance=±5% resistance=220 package="0603 [SMD]"]
  1_K_3 = Resistor [tolerance=±5% resistance=220 package="0603 [SMD]"]
  1_K_4 = Resistor [tolerance=±5% resistance=220 package="0603 [SMD]"]
  1_K_5 = Resistor [tolerance=±5% resistance=220 package="0603 [SMD]"]
  1_K_6 = Resistor [tolerance=±5% resistance=220 package="0603 [SMD]"]
  1_K_7 = Resistor [tolerance=±5% resistance=220 package="0603 [SMD]"]
  1_K_8 = Resistor [tolerance=±5% resistance=220 package="0603 [SMD]"]
  Yellow_LED_1 = LEDs [package=led10mm]
  Yellow_LED_2 = LEDs [package=led10mm]
  Yellow_LED_3 = LEDs [package=led10mm]
  Yellow_LED_4 = LEDs [package=led10mm]
  White_LED_1 = LEDs [package=led10mm]
  White_LED_2 = LEDs [package=led10mm]
  Red_LED_1 = LED - 3mm [color="Red (633nm)" current=0.030 package="3 mm [THT]"]
  Red_LED_2 = LED - 3mm [color="Red (633nm)" current=0.030 package="3 mm [THT]"]

nets:
  GND: Part1.GND, Part2.GND, IR_Left.GND, Buzzer_Left.-, IR_Right.GND, Buzzer_Right.-, HC-SR04.GND, IR_Front_Left.GND, IR_Front_Right.GND, Servomotor.gnd, 10_K.Pin_1
  VCC: Part1.VCC, Part2.5V, IR_Left.Vcc, Buzzer_Left.NC, IR_Right.Vcc, Buzzer_Right.NC, HC-SR04.VCC, IR_Front_Left.Vcc, IR_Front_Right.Vcc, Servomotor.vcc, R1.P$1, U2.C, U3.C, U4.C, U5.C, U6.C, U7.C, U8.C, U9.C
  N1: Part1.CE, Part2.D9_PWM
  N2: Part1.CS, Part2.D10_PWM
  N3: Part1.SCK, Part2.D52/SCK
  N4: Part1.MOSI, Part2.D51/MOSI
  N5: Part1.MISO, Part2.D50/MISO
  N6: Part2.A15, R1.P$2, 10_K.Pin_0
  N7: Part2.A1, IR_Front_Left.Vout
  N8: Part2.A2, IR_Front_Right.Vout
  N9: Part2.A3, HC-SR04.TRIG
  N10: Part2.A4, HC-SR04.ECHO
  N11: Part2.D12_PWM, Buzzer_Right.S
  N12: Part2.D11_PWM, Servomotor.pulse
  N13: Part2.D8_PWM, U1.IN4
  N14: Part2.D2_PWM, IR_Right.Vout
  N15: Part2.D3_PWM, U1.IN1
  N16: Part2.D4_PWM, U1.IN2
  N17: Part2.D5_PWM, U1.ENA
  N18: Part2.D6_PWM, U1.ENB
  N19: Part2.D7_PWM, U1.IN3
  N20: Part2.D26, 1_K.Pin_0, 1_K_2.Pin_0, 1_K_3.Pin_0, 1_K_4.Pin_0, 1_K_5.Pin_0, 1_K_6.Pin_0, 1_K_7.Pin_0, 1_K_8.Pin_0
  N21: Part2.D32, IR_Left.Vout
  N22: Part2.D34, Buzzer_Left.S
  N23: U1.OUT1, M1.pin_1, M2.pin_1
  N24: U1.OUT2, M1.pin_2, M2.pin_2
  N25: U1.OUT3, M3.pin_1, M4.pin_1
  N26: U1.OUT4, M3.pin_2, M4.pin_2
  N27: U2.B, 1_K.Pin_1
  N28: U2.E, Yellow_LED_1.A
  N29: U3.B, 1_K_2.Pin_1
  N30: U3.E, White_LED_1.A
  N31: U4.B, 1_K_3.Pin_1
  N32: U4.E, White_LED_2.A
  N33: U5.B, 1_K_4.Pin_1
  N34: U5.E, Yellow_LED_2.A
  N35: U6.B, 1_K_5.Pin_1
  N36: U6.E, Yellow_LED_3.A
  N37: U7.B, 1_K_6.Pin_1
  N38: U7.E, Red_LED_1.anode
  N39: U8.B, 1_K_7.Pin_1
  N40: U8.E, Red_LED_2.anode
  N41: U9.B, 1_K_8.Pin_1
  N42: U9.E, Yellow_LED_4.A
  GND_2: Yellow_LED_1.C, Yellow_LED_2.C, Yellow_LED_3.C, Yellow_LED_4.C, White_LED_1.C, White_LED_2.C, Red_LED_1.cathode, Red_LED_2.cathode
